// Logisim project Pipelined Processor Final Version.circ as structural Verilog: 11 circuits, main circuit main
module main (
  output [15:0] out_1,
  output [15:0] out_2,
  output [15:0] out_3,
  output [15:0] out_4,
  output [15:0] out_5,
  output [15:0] out_6,
  output [15:0] out_7,
  output [15:0] out_8,
  output [15:0] Writing_Result
);

  wire ALU_Control_beq_bne, ALUSrc, and_1_out, BEQ_BNE, Clk, Dis_IR, ex_1_memwr_2, Ex_MemRd, EX_RegWr, ExtOp,
       Kill1, Kill2, LessFlag, Main_Control_alusrc, Main_Control_memrd, Main_Control_memwr,
       Main_Control_regwr, MEM_RegWr, MemRd, MemWr, movnFlag, movzFlag, not_1_out, or_1_out, RegDst, RegWr,
       stall_mux_1_alusrc_2, stall_mux_1_beq_bne_2, stall_mux_1_memrd_2, stall_mux_1_memwr_2,
       stall_mux_1_regwr_2, ZeroFlag;
  wire [1:0] ex_1_wbdata_2, Fow_A, Fow_B, Main_Control_wbdata, stall_mux_1_wbdata_2, W_1_7, WBdata;
  wire [2:0] Funct, multiplexer_3_out, multiplexer_4_out, PCSrc, Rd2, Rd3, Rd4, Rs, Rt;
  wire [3:0] ALU_Control_aluop, ALUOp, Opcode, stall_mux_1_aluop_2;
  wire [11:0] adder_2_out, bit_extender_1_out, bit_extender_2_out, BTA_q, immd, multiplexer_1_out, NPC_q, PC,
       PCNext, shifter_1_out;
  wire [11:9] Inst_q;
  wire [15:0] ALU_result, B_q, bit_extender_3_out, bit_extender_4_out, bit_extender_5_out,
       bit_extender_6_out, BusA_Reg_Rs, D_q, file_register_1_busa, file_register_1_busb, Imm_q,
       multiplexer_2_out, multiplexer_6_out, multiplexer_7_out, multiplexer_8_out, multiplexer_9_out, R_q,
       ram_1_data, ram_2_data, WR_data;

  Multiplexer #(.select(3), .width(12), .enable("false")) multiplexer_1 (
    .in0(PCNext), .in1({Inst_q, Rs, Rt, Funct}), .in2(BTA_q), .in3(BusA_Reg_Rs[11:0]),
    .in4(BusA_Reg_Rs[11:0]), .out(multiplexer_1_out), .sel(PCSrc));  // open: in5, in6, in7
  Register #(.width(12)) register_1 (.D(multiplexer_1_out), .Q(PC), .clk(Clk), .clr(Dis_IR));  // open: en
  not not_1 (not_1_out, Opcode[1]);
  Adder #(.width(12)) adder_1 (.a(12'h1), .b(PC), .out(PCNext));  // open: cin, cout
  Clock clock_1 (.out(Clk));
  PC_Control PC_Control (
    .Opcode(Opcode), .ZeroFlag(ZeroFlag), .LessFlag(LessFlag), .PCSrc(PCSrc), .Funct(Funct), .Kill2(Kill2),
    .Kill1(Kill1));
  and and_1 (and_1_out, Opcode[0], Opcode[1], Opcode[2], Opcode[3]);
  nor nor_1 (W_1_7[1], and_1_out, W_1_7[0]);
  and and_2 (W_1_7[0], Opcode[0], not_1_out, Opcode[2], Opcode[3]);
  RAM #(.addrWidth(12), .dataWidth(16)) ram_1 (.addr(PC), .data(ram_1_data), .clk(Clk));  // open: sel, ld, clr
  Register #(.width(12)) NPC (.D(PC), .Q(NPC_q), .clk(Clk));  // open: en, clr
  Register #(.width(16)) Inst (
    .D(multiplexer_2_out), .Q({Opcode, Inst_q, Rs, Rt, Funct}), .clk(Clk), .clr(Dis_IR));  // open: en
  Multiplexer #(.width(16), .enable("false")) multiplexer_2 (
    .in0(ram_1_data), .in1({16{1'b0}}), .out(multiplexer_2_out), .sel(Kill1));
  Raw_Hazard_Detection raw_hazard_detection_1 (
    .Rs(Rs), .Rt(Rt), .ForwardA(Fow_A), .Stall(Dis_IR), .MEM_RegWr(MEM_RegWr), .EX_RegWr(EX_RegWr),
    .WB_RegWr(RegWr), .Rd3(Rd3), .Rd4(Rd4), .Ex_MemRd(Ex_MemRd), .Rd2(Rd2), .ForwardB(Fow_B));
  assign bit_extender_1_out = {{6{1'b0}}, {Rt, Funct}};  // Bit_Extender bit_extender_1
  assign bit_extender_2_out = {{6{Rt[2]}}, {Rt, Funct}};  // Bit_Extender bit_extender_2
  Multiplexer #(.select(2), .width(3), .enable("false")) multiplexer_3 (
    .in0(3'b111), .in1(3'b001), .in2(Inst_q), .in3(Inst_q), .out(multiplexer_3_out), .sel(W_1_7));
  Multiplexer #(.width(3), .enable("false")) multiplexer_4 (
    .in0(Inst_q), .in1(Rt), .out(multiplexer_4_out), .sel(RegDst));
  Main_Control Main_Control (
    .Opcode(Opcode), .RegDst(RegDst), .MemWr(Main_Control_memwr), .MemRd(Main_Control_memrd), .ExtOp(ExtOp),
    .ALUSrc(Main_Control_alusrc), .Funct(Funct), .WBdata(Main_Control_wbdata), .movnFlag(movnFlag),
    .movzFlag(movzFlag), .RegWr(Main_Control_regwr));
  ALU_Control ALU_Control (.Opcode(Opcode), .Funct(Funct), .ALUOp(ALU_Control_aluop), .BEQ_BNE(ALU_Control_beq_bne));
  Multiplexer #(.width(12), .enable("false")) multiplexer_5 (
    .in0(bit_extender_1_out), .in1(bit_extender_2_out), .out(immd), .sel(ExtOp));
  Adder #(.width(12)) adder_2 (.a(NPC_q), .b(immd), .out(adder_2_out));  // open: cin, cout
  assign bit_extender_3_out = {{4{1'b0}}, immd};  // Bit_Extender bit_extender_3
  Multiplexer #(.width(16), .enable("false")) multiplexer_6 (
    .in0(bit_extender_3_out), .in1(bit_extender_4_out), .out(multiplexer_6_out), .sel(ExtOp));
  assign bit_extender_4_out = {{4{immd[11]}}, immd};  // Bit_Extender bit_extender_4
  File_Register file_register_1 (
    .BusW(Writing_Result), .RegWrite(RegWr), .RA(Rs), .BusA(file_register_1_busa),
    .BusB(file_register_1_busb), .RW(Rd4), .Clock(Clk), .RB(multiplexer_4_out), .out_8(out_2), .out_9(out_3),
    .out_10(out_4), .out_11(out_5), .out_12(out_6), .out_13(out_7), .out_14(out_8), .out_7(out_1));
  Stall_Mux stall_mux_1 (
    .RegWr(Main_Control_regwr), .ALUSrc(Main_Control_alusrc), .MemRd(Main_Control_memrd),
    .MemWr(Main_Control_memwr), .WBdata(Main_Control_wbdata), .ALUOp(ALU_Control_aluop),
    .BEQ_BNE(ALU_Control_beq_bne), .Stall(or_1_out), .RegWr_2(stall_mux_1_regwr_2),
    .ALUSrc_2(stall_mux_1_alusrc_2), .MemRd_2(stall_mux_1_memrd_2), .MemWr_2(stall_mux_1_memwr_2),
    .WBdata_2(stall_mux_1_wbdata_2), .ALUOp_2(stall_mux_1_aluop_2), .BEQ_BNE_2(stall_mux_1_beq_bne_2));
  or or_1 (or_1_out, Kill2, Dis_IR);
  Multiplexer #(.select(2), .width(16), .enable("false")) multiplexer_7 (
    .in0(file_register_1_busa), .in1(ALU_result), .in2(WR_data), .in3(Writing_Result),
    .out(multiplexer_7_out), .sel(Fow_A));
  Multiplexer #(.select(2), .width(16), .enable("false")) multiplexer_8 (
    .in0(file_register_1_busb), .in1(ALU_result), .in2(WR_data), .in3(Writing_Result),
    .out(multiplexer_8_out), .sel(Fow_B));
  Register #(.width(12)) BTA (.D(adder_2_out), .Q(BTA_q), .clk(Clk));  // open: en, clr
  Register #(.width(16)) Imm (.D(multiplexer_6_out), .Q(Imm_q), .clk(Clk));  // open: en, clr
  Register #(.width(16)) A (.D(multiplexer_7_out), .Q(BusA_Reg_Rs), .clk(Clk));  // open: en, clr
  Register #(.width(16)) B (.D(multiplexer_8_out), .Q(B_q), .clk(Clk));  // open: en, clr
  Register #(.width(3)) u_Rd2 (.D(multiplexer_3_out), .Q(Rd2), .clk(Clk));  // open: en, clr
  EX ex_1 (
    .RegWr(stall_mux_1_regwr_2), .ALUSrc(stall_mux_1_alusrc_2), .MemRd(stall_mux_1_memrd_2),
    .MemWr(stall_mux_1_memwr_2), .WBdata(stall_mux_1_wbdata_2), .ALUOp(stall_mux_1_aluop_2),
    .BEQ_BNE(stall_mux_1_beq_bne_2), .Clk(Clk), .RegWr_2(EX_RegWr), .ALUSrc_2(ALUSrc), .MemRd_2(Ex_MemRd),
    .MemWr_2(ex_1_memwr_2), .WBdata_2(ex_1_wbdata_2), .ALUOp_2(ALUOp), .BEQ_BNE_2(BEQ_BNE));
  Multiplexer #(.width(16), .enable("false")) multiplexer_9 (
    .in0(B_q), .in1(Imm_q), .out(multiplexer_9_out), .sel(ALUSrc));
  ALU alu_1 (
    .ALUOp(ALUOp), .A(BusA_Reg_Rs), .B(multiplexer_9_out), .ALUResult(ALU_result), .ZeroFlag(ZeroFlag),
    .LessFlag(LessFlag), .movnFlag(movnFlag), .movzFlag(movzFlag));
  Register #(.width(16)) R (.D(ALU_result), .Q(R_q), .clk(Clk));  // open: en, clr
  Register #(.width(16)) D (.D(B_q), .Q(D_q), .clk(Clk));  // open: en, clr
  Register #(.width(3)) u_Rd3 (.D(Rd2), .Q(Rd3), .clk(Clk));  // open: en, clr
  MEM MEM (
    .MemRd(Ex_MemRd), .MemWr(ex_1_memwr_2), .WBdata(ex_1_wbdata_2), .RegWr(EX_RegWr), .Clk(Clk),
    .MemRd_2(MemRd), .MemWr_2(MemWr), .WBdata_2(WBdata), .RegWr_2(MEM_RegWr));
  Shifter_part #(.width(12)) shifter_1 (.in(immd), .\dist (4'b0100), .out(shifter_1_out));
  assign bit_extender_5_out = {{4{1'b0}}, shifter_1_out};  // Bit_Extender bit_extender_5
  assign bit_extender_6_out = {{4{1'b0}}, PCNext};  // Bit_Extender bit_extender_6
  RAM #(.addrWidth(16), .dataWidth(16), .bus("separate")) ram_2 (
    .addr(R_q), .din(D_q), .data(ram_2_data), .str(MemWr), .clk(Clk), .ld(MemRd));  // open: sel, clr
  Multiplexer #(.select(2), .width(16), .enable("false")) multiplexer_10 (
    .in0(R_q), .in1(bit_extender_6_out), .in2(bit_extender_5_out), .in3(ram_2_data), .out(WR_data),
    .sel(WBdata));
  Register #(.width(16)) Data (.D(WR_data), .Q(Writing_Result), .clk(Clk));  // open: en, clr
  Register #(.width(3)) u_Rd4 (.D(Rd3), .Q(Rd4), .clk(Clk));  // open: en, clr
  Register #(.width(1)) WB (.D(MEM_RegWr), .Q(RegWr), .clk(Clk));  // open: en, clr

  // Other names for the same wires on the sheet: BusW_new[15:0] = Writing_Result; R0[15:0] = out_8; R1[15:0] = out_7;
  //   R2[15:0] = out_6; R3[15:0] = out_5; R4[15:0] = out_4; R5[15:0] = out_3; R6[15:0] = out_2; R7[15:0] = out_1;
  //   Rd_new[2:0] = Rd4; Dis_PC = Dis_IR; Stall = Dis_IR; WB_RegWr = RegWr

  // Notes on the sheet:
  //   Registers Values
  //   LUI
  //   JALR
endmodule

module ALU (
  input  [3:0] ALUOp,
  input  [15:0] A,
  input  [15:0] B,
  output [15:0] ALUResult,
  output ZeroFlag,
  output LessFlag,
  output movnFlag,
  output movzFlag
);

  wire comparator_1_eq, comparator_1_gt, comparator_2_eq, comparator_2_gt, or_2_out, or_3_out;
  wire [15:0] adder_1_out, and_1_out, and_2_out, and_3_out, bit_extender_1_out, bit_extender_2_out,
       bit_extender_3_out, bit_extender_4_out, not_1_out, or_1_out, shifter_1_out, shifter_2_out,
       shifter_3_out, shifter_4_out, subtractor_1_out, undriven, undriven_2, xor_1_out;

  assign or_1_out = A | B;  // OR_Gate or_1, 16 bits wide
  assign and_1_out = A & B;  // AND_Gate and_1, 16 bits wide
  assign xor_1_out = A ^ B;  // XOR_Gate xor_1, 16 bits wide
  Adder #(.width(16)) adder_1 (.a(A), .b(B), .out(adder_1_out));  // open: cin, cout
  Subtractor #(.width(16)) subtractor_1 (.a(A), .b(B), .out(subtractor_1_out));  // open: bin, bout
  assign not_1_out = ~and_1_out;  // NOT_Gate not_1, 16 bits wide
  Shifter_part #(.width(16)) shifter_1 (.in(A), .\dist (B[3:0]), .out(shifter_1_out));
  Shifter_part #(.width(16), .shift("lr")) shifter_2 (.in(A), .\dist (B[3:0]), .out(shifter_2_out));
  Shifter_part #(.width(16), .shift("ar")) shifter_3 (.in(A), .\dist (B[3:0]), .out(shifter_3_out));
  Shifter_part #(.width(16), .shift("rr")) shifter_4 (.in(A), .\dist (B[3:0]), .out(shifter_4_out));
  Comparator #(.width(16)) comparator_1 (.a(A), .b(B), .gt(comparator_1_gt), .eq(comparator_1_eq));  // open: lt
  Comparator #(.width(16), .mode("unsigned")) comparator_2 (
    .a(A), .b(B), .gt(comparator_2_gt), .eq(comparator_2_eq));  // open: lt
  or or_2 (or_2_out, comparator_1_gt, comparator_1_eq);
  or or_3 (or_3_out, comparator_2_gt, comparator_2_eq);
  assign bit_extender_1_out = {{15{1'b0}}, or_2_out};  // Bit_Extender bit_extender_1
  assign bit_extender_2_out = {{15{1'b0}}, or_3_out};  // Bit_Extender bit_extender_2
  Multiplexer #(.select(4), .width(16), .enable("false")) multiplexer_1 (
    .in0(or_1_out), .in1(and_1_out), .in2(not_1_out), .in3(xor_1_out), .in4(adder_1_out),
    .in5(subtractor_1_out), .in6(shifter_1_out), .in7(shifter_2_out), .in8(shifter_3_out),
    .in9(shifter_4_out), .in10(bit_extender_1_out), .in11(bit_extender_2_out), .in12(and_2_out),
    .in13(and_3_out), .in14(undriven), .in15(undriven_2), .out(ALUResult), .sel(ALUOp));
  Comparator #(.width(16)) comparator_3 (
    .a(subtractor_1_out), .b({16{1'b0}}), .eq(ZeroFlag), .lt(LessFlag));  // open: gt
  or or_4 (movnFlag, B[0], B[1], B[2], B[3], B[4], B[5], B[6], B[7], B[8], B[9], B[10], B[11], B[12], B[13], B[14], B[15]);
  not not_2 (movzFlag, movnFlag);
  assign bit_extender_3_out = {{15{movzFlag}}, movzFlag};  // Bit_Extender bit_extender_3
  assign bit_extender_4_out = {{15{movnFlag}}, movnFlag};  // Bit_Extender bit_extender_4
  assign and_2_out = A & bit_extender_3_out;  // AND_Gate and_2, 16 bits wide
  assign and_3_out = bit_extender_4_out & A;  // AND_Gate and_3, 16 bits wide

  // Other names for the same wires on the sheet: Rs[15:0] = A; Rt[15:0] = B
endmodule

module Shifter (
  input  [15:0] Data,
  input  [3:0] Shift_amount,
  input  [1:0] Shift_Op,
  output [15:0] Data_out
);

  wire [15:0] shifter_1_out, shifter_2_out, shifter_3_out, shifter_4_out;

  Shifter_part #(.width(16)) shifter_1 (.in(Data), .\dist (Shift_amount), .out(shifter_1_out));
  Shifter_part #(.width(16), .shift("lr")) shifter_2 (.in(Data), .\dist (Shift_amount), .out(shifter_2_out));
  Shifter_part #(.width(16), .shift("ar")) shifter_3 (.in(Data), .\dist (Shift_amount), .out(shifter_3_out));
  Shifter_part #(.width(16), .shift("rr")) shifter_4 (.in(Data), .\dist (Shift_amount), .out(shifter_4_out));
  Multiplexer #(.select(2), .width(16), .enable("false")) multiplexer_1 (
    .in0(shifter_1_out), .in1(shifter_2_out), .in2(shifter_3_out), .in3(shifter_4_out), .out(Data_out),
    .sel(Shift_Op));
endmodule

module File_Register (
  input  [2:0] RA,
  input  [2:0] RW,
  input  [15:0] BusW,
  input  RegWrite,
  input  [2:0] RB,
  input  Clock,
  output [15:0] out_7,
  output [15:0] out_8,
  output [15:0] out_9,
  output [15:0] out_10,
  output [15:0] out_11,
  output [15:0] out_12,
  output [15:0] out_13,
  output [15:0] out_14,
  output [15:0] BusA,
  output [15:0] BusB
);

  wire and_1_out, and_2_out, and_3_out, and_4_out, and_5_out, and_6_out, and_7_out, decoder_1_out0,
       decoder_1_out1, decoder_1_out2, decoder_1_out3, decoder_1_out4, decoder_1_out5, decoder_1_out6,
       decoder_1_out7;

  Decoder #(.select(3), .enable("false")) decoder_1 (
    .out0(decoder_1_out0), .out1(decoder_1_out1), .out2(decoder_1_out2), .out3(decoder_1_out3),
    .out4(decoder_1_out4), .out5(decoder_1_out5), .out6(decoder_1_out6), .out7(decoder_1_out7), .sel(RW));
  Register #(.width(16)) R0 (.D({16{1'b0}}), .Q(out_14), .clk(Clock));  // open: en, clr
  Register #(.width(16)) R1 (.D(BusW), .en(and_1_out), .Q(out_13), .clk(Clock));  // open: clr
  and and_1 (and_1_out, decoder_1_out1, RegWrite);
  Register #(.width(16)) R2 (.D(BusW), .en(and_2_out), .Q(out_12), .clk(Clock));  // open: clr
  and and_2 (and_2_out, decoder_1_out2, RegWrite);
  Register #(.width(16)) R3 (.D(BusW), .en(and_3_out), .Q(out_11), .clk(Clock));  // open: clr
  and and_3 (and_3_out, decoder_1_out3, RegWrite);
  Register #(.width(16)) R4 (.D(BusW), .en(and_4_out), .Q(out_10), .clk(Clock));  // open: clr
  and and_4 (and_4_out, decoder_1_out4, RegWrite);
  Register #(.width(16)) R5 (.D(BusW), .en(and_5_out), .Q(out_9), .clk(Clock));  // open: clr
  and and_5 (and_5_out, decoder_1_out5, RegWrite);
  Register #(.width(16)) R6 (.D(BusW), .en(and_6_out), .Q(out_8), .clk(Clock));  // open: clr
  and and_6 (and_6_out, decoder_1_out6, RegWrite);
  Register #(.width(16)) R7 (.D(BusW), .en(and_7_out), .Q(out_7), .clk(Clock));  // open: clr
  and and_7 (and_7_out, decoder_1_out7, RegWrite);
  Multiplexer #(.select(3), .width(16), .enable("false")) multiplexer_1 (
    .in0(out_14), .in1(out_13), .in2(out_12), .in3(out_11), .in4(out_10), .in5(out_9), .in6(out_8),
    .in7(out_7), .out(BusA), .sel(RA));
  Multiplexer #(.select(3), .width(16), .enable("false")) multiplexer_2 (
    .in0(out_14), .in1(out_13), .in2(out_12), .in3(out_11), .in4(out_10), .in5(out_9), .in6(out_8),
    .in7(out_7), .out(BusB), .sel(RB));

  // Other names for the same wires on the sheet: R0[15:0] = out_14; R1[15:0] = out_13; R2[15:0] = out_12;
  //   R3[15:0] = out_11; R4[15:0] = out_10; R5[15:0] = out_9; R6[15:0] = out_8; R7[15:0] = out_7
endmodule

module PC_Control (
  input  [3:0] Opcode,
  input  ZeroFlag,
  input  LessFlag,
  input  [2:0] Funct,
  output Kill2,
  output Kill1,
  output [2:0] PCSrc
);

  wire and_1_out, and_2_out, and_5_out, and_6_out, and_7_out, and_8_out, and_9_out, and_10_out, and_11_out,
       decoder_1_out1, decoder_1_out7, decoder_1_out8, decoder_1_out9, decoder_1_out10, decoder_1_out11,
       decoder_1_out12, JAL, JALR, JALR1, Jmp, JR, JR1, Jump, not_1_out, not_2_out, or_3_out;

  Decoder #(.select(4), .enable("false")) decoder_1 (
    .out1(decoder_1_out1), .out7(decoder_1_out7), .out8(decoder_1_out8), .out9(decoder_1_out9),
    .out10(decoder_1_out10), .out11(decoder_1_out11), .out12(decoder_1_out12), .out14(Jump), .out15(JAL),
    .sel(Opcode));  // open: out0, out2, out3, out4, out5, out6, out13
  not not_1 (not_1_out, ZeroFlag);
  and and_1 (and_1_out, Funct[0], Funct[1], Funct[2]);
  and and_2 (and_2_out, ~Funct[0], Funct[1], Funct[2]);  // AND_Gate
  not not_2 (not_2_out, LessFlag);
  and and_3 (JR, decoder_1_out1, and_2_out);
  and and_4 (JALR, decoder_1_out1, and_1_out);
  and and_5 (and_5_out, ZeroFlag, decoder_1_out12);
  and and_6 (and_6_out, LessFlag, decoder_1_out12);
  and and_7 (and_7_out, LessFlag, decoder_1_out11);
  and and_8 (and_8_out, not_2_out, decoder_1_out10);
  and and_9 (and_9_out, not_2_out, not_1_out, decoder_1_out9);
  and and_10 (and_10_out, decoder_1_out8, ZeroFlag);
  and and_11 (and_11_out, not_1_out, decoder_1_out7);
  or or_1 (Kill2, and_5_out, and_6_out, and_7_out, and_8_out, and_9_out, and_10_out, and_11_out);
  Multiplexer #(.select(4), .width(3), .enable("false")) multiplexer_1 (
    .in0(3'b000), .in1(3'b001), .in2(3'b010), .in4(3'b011), .in8(3'b100), .out(PCSrc),
    .sel({JR1, JALR1, Kill2, Jmp}));  // open: in3, in5, in6, in7, in9, in10, in11, in12, in13, in14, in15
  or or_2 (Kill1, Kill2, JR, JALR, Jmp);
  and and_12 (JR1, ~Kill2, JR);  // AND_Gate
  and and_13 (JALR1, ~Kill2, JALR);  // AND_Gate
  and and_14 (Jmp, ~Kill2, or_3_out);  // AND_Gate
  or or_3 (or_3_out, JAL, Jump);

  // Other names for the same wires on the sheet: Branch = Kill2
endmodule

module Main_Control (
  input  [3:0] Opcode,
  input  movnFlag,
  input  movzFlag,
  input  [2:0] Funct,
  output MemWr,
  output MemRd,
  output [1:0] WBdata,
  output RegDst,
  output ExtOp,
  output ALUSrc,
  output RegWr
);

  wire _0, _1, _2, _3, _4, _13, _15, and_1_out, and_2_out, and_3_out, and_4_out, and_5_out, and_6_out,
       and_7_out, and_9_out, and_10_out, and_11_out, and_12_out, and_14_out, movOp, MovSignal,
       multiplexer_1_out, not_1_out, op1, or_2_out, or_3_out, or_5_out, or_6_out;

  or or_1 (RegDst, _0, _13, _1);
  or or_2 (or_2_out, _0, _1, _2, _3, _4, MemRd, _13, _15);
  and and_1 (and_1_out, ~Funct[0], Funct[1], Funct[2]);  // AND_Gate
  and and_2 (and_2_out, Funct[0], Funct[1], Funct[2]);
  not not_1 (not_1_out, Opcode[1]);
  Decoder #(.select(4), .enable("false")) decoder_1 (
    .out0(_0), .out1(_1), .out2(_2), .out3(_3), .out4(_4), .out5(MemWr), .out6(MemRd), .out13(_13),
    .out15(_15), .sel(Opcode));  // open: out7, out8, out9, out10, out11, out12, out14
  Multiplexer #(.enable("false")) multiplexer_1 (.in0(or_2_out), .in1(MovSignal), .out(multiplexer_1_out), .sel(movOp));
  and and_3 (and_3_out, and_1_out, op1);
  and and_4 (and_4_out, Opcode[0], Opcode[1], Opcode[2], Opcode[3]);
  and and_5 (and_5_out, Opcode[0], ~Opcode[1], ~Opcode[2], ~Opcode[3]);  // AND_Gate
  and and_6 (and_6_out, and_5_out, and_2_out);
  and and_7 (and_7_out, Opcode[0], not_1_out, Opcode[2], Opcode[3]);
  and and_8 (RegWr, multiplexer_1_out, ~and_3_out);  // AND_Gate
  or or_3 (or_3_out, and_4_out, and_6_out);
  Priority_Encoder #(.select(2), .disabled(0)) priority_encoder_1 (
    .in0(1'b1), .in1(or_3_out), .in2(and_7_out), .in3(MemRd), .out(WBdata));  // open: gs, en_out, en_in
  nor nor_1 (ExtOp, _2, _3, _13);
  and and_9 (and_9_out, ~Funct[0], ~Funct[1], Funct[2]);  // AND_Gate
  and and_10 (and_10_out, Funct[0], ~Funct[1], Funct[2]);  // AND_Gate
  and and_11 (and_11_out, op1, movnFlag, and_10_out);
  and and_12 (and_12_out, op1, movzFlag, and_9_out);
  and and_13 (op1, Opcode[0], ~Opcode[1], ~Opcode[2], ~Opcode[3]);  // AND_Gate
  or or_4 (ALUSrc, _2, _3, _4, MemWr, MemRd, _13);
  or or_5 (or_5_out, and_11_out, and_12_out);
  or or_6 (or_6_out, and_9_out, and_10_out);
  and and_14 (and_14_out, or_6_out, op1);
  and and_15 (movOp, op1, or_6_out);
  and and_16 (MovSignal, or_5_out, and_14_out);

  // Other names for the same wires on the sheet: _5 = MemWr; _6 = MemRd
endmodule

module ALU_Control (
  input  [3:0] Opcode,
  input  [2:0] Funct,
  output BEQ_BNE,
  output [3:0] ALUOp
);

  wire and_1_out, and_2_out, and_3_out, and_4_out, and_5_out, and_6_out, and_7_out, and_8_out, and_9_out,
       and_10_out, and_11_out, not_1_out, not_2_out, not_3_out, not_4_out, not_5_out, not_6_out, not_7_out,
       not_8_out, not_9_out, not_10_out, not_11_out, not_12_out, not_13_out, not_14_out, not_15_out,
       not_16_out, not_17_out, not_18_out, not_19_out, not_20_out, not_21_out, not_22_out, not_23_out,
       not_24_out, not_25_out, not_26_out, not_27_out;

  not not_1 (not_1_out, Opcode[3]);
  not not_2 (not_2_out, Opcode[2]);
  not not_3 (not_3_out, Opcode[1]);
  not not_4 (not_4_out, Opcode[3]);
  not not_5 (not_5_out, Opcode[2]);
  not not_6 (not_6_out, Opcode[1]);
  not not_7 (not_7_out, Opcode[3]);
  not not_8 (not_8_out, Opcode[2]);
  not not_9 (not_9_out, Opcode[1]);
  not not_10 (not_10_out, Opcode[1]);
  not not_11 (not_11_out, Opcode[1]);
  not not_12 (not_12_out, Funct[1]);
  not not_13 (not_13_out, Opcode[1]);
  not not_14 (not_14_out, Funct[1]);
  not not_15 (not_15_out, Opcode[3]);
  not not_16 (not_16_out, Opcode[2]);
  not not_17 (not_17_out, Opcode[1]);
  not not_18 (not_18_out, Opcode[0]);
  not not_19 (not_19_out, Opcode[3]);
  not not_20 (not_20_out, Opcode[2]);
  not not_21 (not_21_out, Opcode[1]);
  not not_22 (not_22_out, Funct[2]);
  not not_23 (not_23_out, Funct[1]);
  not not_24 (not_24_out, Opcode[2]);
  not not_25 (not_25_out, Opcode[1]);
  not not_26 (not_26_out, Opcode[2]);
  not not_27 (not_27_out, Opcode[0]);
  and and_1 (and_1_out, not_1_out, not_2_out, not_3_out, Funct[2], Funct[1]);
  and and_2 (and_2_out, not_4_out, not_5_out, not_6_out, Opcode[0], Funct[1]);
  and and_3 (and_3_out, not_7_out, not_8_out, not_9_out, Opcode[0], Funct[2]);
  and and_4 (and_4_out, Opcode[3], Opcode[2], not_10_out, Opcode[0]);
  and and_5 (and_5_out, not_11_out, Funct[2], not_12_out);
  and and_6 (and_6_out, not_13_out, Opcode[0], not_14_out);
  and and_7 (and_7_out, not_15_out, not_16_out, not_17_out, not_18_out, Funct[1]);
  and and_8 (and_8_out, not_19_out, not_20_out, not_21_out, Opcode[0], not_22_out, not_23_out);
  and and_9 (and_9_out, not_24_out, not_25_out, Funct[0]);
  and and_10 (and_10_out, not_26_out, Opcode[1], not_27_out);
  and and_11 (and_11_out, Opcode[2], Opcode[1], Opcode[0]);
  or or_1 (ALUOp[3], and_1_out, and_2_out, and_3_out, and_4_out);
  or or_2 (ALUOp[2], and_5_out, and_6_out, Opcode[2], Opcode[3]);
  or or_3 (ALUOp[1], and_7_out, and_8_out);
  or or_4 (ALUOp[0], and_9_out, and_10_out, and_11_out, Opcode[3]);
  and and_12 (BEQ_BNE, ~ALUOp[3], ALUOp[2], ~ALUOp[1], ALUOp[0]);  // AND_Gate
endmodule

module EX (
  input  RegWr,
  input  ALUSrc,
  input  MemRd,
  input  MemWr,
  input  [1:0] WBdata,
  input  [3:0] ALUOp,
  input  BEQ_BNE,
  input  Clk,
  output RegWr_2,
  output ALUSrc_2,
  output MemRd_2,
  output MemWr_2,
  output [1:0] WBdata_2,
  output [3:0] ALUOp_2,
  output BEQ_BNE_2
);

  Register #(.width(1)) register_1 (.D(RegWr), .Q(RegWr_2), .clk(Clk));  // open: en, clr
  Register #(.width(1)) register_2 (.D(ALUSrc), .Q(ALUSrc_2), .clk(Clk));  // open: en, clr
  Register #(.width(1)) register_3 (.D(MemRd), .Q(MemRd_2), .clk(Clk));  // open: en, clr
  Register #(.width(1)) register_4 (.D(MemWr), .Q(MemWr_2), .clk(Clk));  // open: en, clr
  Register #(.width(2)) register_5 (.D(WBdata), .Q(WBdata_2), .clk(Clk));  // open: en, clr
  Register #(.width(4)) register_6 (.D(ALUOp), .Q(ALUOp_2), .clk(Clk));  // open: en, clr
  Register #(.width(1)) register_7 (.D(BEQ_BNE), .Q(BEQ_BNE_2), .clk(Clk));  // open: en, clr
endmodule

module MEM (
  input  MemRd,
  input  MemWr,
  input  [1:0] WBdata,
  input  RegWr,
  input  Clk,
  output MemRd_2,
  output MemWr_2,
  output [1:0] WBdata_2,
  output RegWr_2
);

  Register #(.width(1)) register_1 (.D(MemRd), .Q(MemRd_2), .clk(Clk));  // open: en, clr
  Register #(.width(1)) register_2 (.D(MemWr), .Q(MemWr_2), .clk(Clk));  // open: en, clr
  Register #(.width(2)) register_3 (.D(WBdata), .Q(WBdata_2), .clk(Clk));  // open: en, clr
  Register #(.width(1)) register_4 (.D(RegWr), .Q(RegWr_2), .clk(Clk));  // open: en, clr
endmodule

module Stall_Mux (
  input  RegWr,
  input  ALUSrc,
  input  MemRd,
  input  MemWr,
  input  [1:0] WBdata,
  input  [3:0] ALUOp,
  input  BEQ_BNE,
  input  Stall,
  output RegWr_2,
  output ALUSrc_2,
  output MemRd_2,
  output MemWr_2,
  output [1:0] WBdata_2,
  output [3:0] ALUOp_2,
  output BEQ_BNE_2
);

  Multiplexer #(.enable("false")) multiplexer_1 (.in0(RegWr), .in1(1'b0), .out(RegWr_2), .sel(Stall));
  Multiplexer #(.enable("false")) multiplexer_2 (.in0(ALUSrc), .in1(1'b0), .out(ALUSrc_2), .sel(Stall));
  Multiplexer #(.enable("false")) multiplexer_3 (.in0(MemRd), .in1(1'b0), .out(MemRd_2), .sel(Stall));
  Multiplexer #(.enable("false")) multiplexer_4 (.in0(MemWr), .in1(1'b0), .out(MemWr_2), .sel(Stall));
  Multiplexer #(.width(2), .enable("false")) multiplexer_5 (.in0(WBdata), .in1(2'b00), .out(WBdata_2), .sel(Stall));
  Multiplexer #(.width(4), .enable("false")) multiplexer_6 (.in0(ALUOp), .in1(4'b0000), .out(ALUOp_2), .sel(Stall));
  Multiplexer #(.enable("false")) multiplexer_7 (.in0(BEQ_BNE), .in1(1'b0), .out(BEQ_BNE_2), .sel(Stall));
endmodule

// RAW_H_D
module Raw_Hazard_Detection (
  input  [2:0] Rs,
  input  [2:0] Rd2,
  input  EX_RegWr,
  input  MEM_RegWr,
  input  [2:0] Rd3,
  input  Ex_MemRd,
  input  [2:0] Rd4,
  input  WB_RegWr,
  input  [2:0] Rt,
  output [1:0] ForwardA,
  output Stall,
  output [1:0] ForwardB
);

  wire and_1_out, and_2_out, and_3_out, and_4_out, and_5_out, and_6_out, and_7_out, and_8_out, and_9_out,
       and_10_out, and_11_out, and_12_out, and_13_out, and_14_out, not_1_out, not_2_out, not_3_out,
       not_4_out, not_5_out, not_6_out, or_7_out, Rs__0, Rs____Rd2, Rs____Rd3, Rs____Rd4, Rt__0, Rt____Rd2,
       Rt____Rd3, Rt____Rd4;

  or or_1 (Rs__0, Rs[0], Rs[1], Rs[2]);
  or or_2 (Rt__0, Rt[0], Rt[1], Rt[2]);
  Comparator #(.width(3)) comparator_1 (.a(Rd2), .b(Rs), .eq(Rs____Rd2));  // open: gt, lt
  Comparator #(.width(3)) comparator_2 (.a(Rs), .b(Rd3), .eq(Rs____Rd3));  // open: gt, lt
  Comparator #(.width(3)) comparator_3 (.a(Rs), .b(Rd4), .eq(Rs____Rd4));  // open: gt, lt
  Comparator #(.width(3)) comparator_4 (.a(Rd2), .b(Rt), .eq(Rt____Rd2));  // open: gt, lt
  Comparator #(.width(3)) comparator_5 (.a(Rt), .b(Rd3), .eq(Rt____Rd3));  // open: gt, lt
  Comparator #(.width(3)) comparator_6 (.a(Rt), .b(Rd4), .eq(Rt____Rd4));  // open: gt, lt
  and and_1 (and_1_out, Rs__0, Rs____Rd2, EX_RegWr);
  and and_2 (and_2_out, Rs__0, Rs____Rd3, MEM_RegWr);
  and and_3 (and_3_out, Rs__0, Rs____Rd4, WB_RegWr);
  and and_4 (and_4_out, Rt__0, Rt____Rd2, EX_RegWr);
  and and_5 (and_5_out, Rt__0, Rt____Rd3, MEM_RegWr);
  and and_6 (and_6_out, Rt__0, Rt____Rd4, WB_RegWr);
  not not_1 (not_1_out, and_1_out);
  not not_2 (not_2_out, and_1_out);
  not not_3 (not_3_out, and_2_out);
  not not_4 (not_4_out, and_4_out);
  not not_5 (not_5_out, and_4_out);
  not not_6 (not_6_out, and_5_out);
  and and_7 (and_7_out, not_1_out, and_3_out);
  and and_8 (and_8_out, not_2_out, and_2_out);
  and and_9 (and_9_out, not_3_out, and_3_out);
  and and_10 (and_10_out, not_4_out, and_6_out);
  and and_11 (and_11_out, not_5_out, and_5_out);
  and and_12 (and_12_out, not_6_out, and_6_out);
  or or_3 (ForwardA[1], and_7_out, and_8_out);
  or or_4 (ForwardA[0], and_9_out, and_1_out);
  and and_13 (and_13_out, ForwardA[0], ~ForwardA[1]);  // AND_Gate
  and and_14 (and_14_out, ForwardB[0], ~ForwardB[1]);  // AND_Gate
  or or_5 (ForwardB[1], and_10_out, and_11_out);
  or or_6 (ForwardB[0], and_12_out, and_4_out);
  or or_7 (or_7_out, and_13_out, and_14_out);
  and and_15 (Stall, Ex_MemRd, or_7_out);

  // Other names for the same wires on the sheet: FwA[1:0] = ForwardA; FwB[1:0] = ForwardB
endmodule
