// Logisim project Single Cycle Processor.circ as structural Verilog: 7 circuits, main circuit main
module main (
);

  wire ALUSrc, and_1_out, Clk, ExtOp, LessFlag, MemRd, MemWr, not_1_out, RegDst, RegWr, ZeroFlag;
  wire [1:0] PCSrc, W_1_7, WBdata;
  wire [2:0] Funct, multiplexer_2_out, multiplexer_3_out, Rs;
  wire [3:0] ALUOp, Opcode;
  wire [11:0] adder_2_out, bit_extender_1_out, bit_extender_2_out, bit_extender_3_out, immd,
       multiplexer_1_out, PCNext, register_1_q, shifter_1_out;
  wire [11:3] ram_1_data;
  wire [15:0] ALU_aluresult, bit_extender_4_out, bit_extender_5_out, bit_extender_6_out, bit_extender_7_out,
       file_register_1_busa, multiplexer_5_out, multiplexer_6_out, multiplexer_7_out, ram_2_data, Reg_Rs;

  Multiplexer #(.select(2), .width(12), .enable("false")) multiplexer_1 (
    .in0(PCNext), .in1({ram_1_data[11:9], Rs, ram_1_data[5:3], Funct}), .in2(adder_2_out),
    .in3(bit_extender_1_out), .out(multiplexer_1_out), .sel(PCSrc));
  assign bit_extender_1_out = {{9{1'b0}}, Rs};  // Bit_Extender bit_extender_1
  Register #(.width(12)) register_1 (.D(multiplexer_1_out), .Q(register_1_q), .clk(Clk));  // open: en, clr
  Clock clock_1 (.out(Clk));
  PC_Control PC_Control (.Opcode(Opcode), .ZeroFlag(ZeroFlag), .LessFlag(LessFlag), .PCSrc(PCSrc));
  not not_1 (not_1_out, Opcode[1]);
  Adder #(.width(12)) adder_1 (.a(12'h1), .b(register_1_q), .out(PCNext));  // open: cin, cout
  and and_1 (and_1_out, Opcode[0], Opcode[1], Opcode[2], Opcode[3]);
  and and_2 (W_1_7[0], Opcode[0], not_1_out, Opcode[2], Opcode[3]);
  RAM #(.addrWidth(12), .dataWidth(16)) ram_1 (
    .addr(register_1_q), .data({Opcode, ram_1_data[11:9], Rs, ram_1_data[5:3], Funct}), .clk(Clk));  // open: sel, ld, clr
  nor nor_1 (W_1_7[1], and_1_out, W_1_7[0]);
  assign bit_extender_2_out = {{6{ram_1_data[5]}}, {ram_1_data[5:3], Funct}};  // Bit_Extender bit_extender_2
  assign bit_extender_3_out = {{6{1'b0}}, {ram_1_data[5:3], Funct}};  // Bit_Extender bit_extender_3
  Multiplexer #(.select(2), .width(3), .enable("false")) multiplexer_2 (
    .in0(3'b111), .in1(3'b001), .in2(ram_1_data[11:9]), .in3(ram_1_data[11:9]), .out(multiplexer_2_out),
    .sel(W_1_7));
  Multiplexer #(.width(3), .enable("false")) multiplexer_3 (
    .in0(ram_1_data[11:9]), .in1(Rs), .out(multiplexer_3_out), .sel(RegDst));
  Multiplexer #(.width(12), .enable("false")) multiplexer_4 (
    .in0(bit_extender_2_out), .in1(bit_extender_3_out), .out(immd), .sel(ExtOp));
  Main_Control main_control_1 (
    .Opcode(Opcode), .RegDst(RegDst), .MemWr(MemWr), .MemRd(MemRd), .ExtOp(ExtOp), .ALUSrc(ALUSrc),
    .Funct(Funct), .WBdata(WBdata), .RegWr(RegWr));
  assign bit_extender_4_out = {{4{1'b0}}, immd};  // Bit_Extender bit_extender_4
  Multiplexer #(.width(16), .enable("false")) multiplexer_5 (
    .in0(bit_extender_4_out), .in1(bit_extender_5_out), .out(multiplexer_5_out), .sel(ExtOp));
  assign bit_extender_5_out = {{4{immd[11]}}, immd};  // Bit_Extender bit_extender_5
  File_Register file_register_1 (
    .BusW(multiplexer_7_out), .RegWrite(RegWr), .RA(ram_1_data[5:3]), .RB(multiplexer_3_out),
    .BusA(file_register_1_busa), .BusB(Reg_Rs), .RW(multiplexer_2_out), .Clock(Clk));
  Adder #(.width(12)) adder_2 (.a(PCNext), .b(immd), .out(adder_2_out));  // open: cin, cout
  Multiplexer #(.width(16), .enable("false")) multiplexer_6 (
    .in0(Reg_Rs), .in1(multiplexer_5_out), .out(multiplexer_6_out), .sel(ALUSrc));
  ALU ALU (
    .A(file_register_1_busa), .B(multiplexer_6_out), .ALUResult(ALU_aluresult), .ZeroFlag(LessFlag),
    .LessFlag(ZeroFlag));  // open: ALUOp
  ALU_Control alu_control_1 (.Opcode(Opcode), .Funct(Funct), .ALUOp(ALUOp));
  Shifter_part #(.width(12)) shifter_1 (.in(immd), .\dist (4'b0100), .out(shifter_1_out));
  assign bit_extender_6_out = {{4{1'b0}}, shifter_1_out};  // Bit_Extender bit_extender_6
  assign bit_extender_7_out = {{4{1'b0}}, PCNext};  // Bit_Extender bit_extender_7
  RAM #(.addrWidth(16), .dataWidth(16), .bus("separate")) ram_2 (
    .addr(ALU_aluresult), .din(Reg_Rs), .data(ram_2_data), .str(MemWr), .clk(Clk), .ld(MemRd));  // open: sel, clr
  Multiplexer #(.select(2), .width(16), .enable("false")) multiplexer_7 (
    .in0(bit_extender_6_out), .in1(bit_extender_7_out), .in2(ALU_aluresult), .in3(ram_2_data),
    .out(multiplexer_7_out), .sel(WBdata));
endmodule

module ALU (
  input  [3:0] ALUOp,
  input  [15:0] A,
  input  [15:0] B,
  output [15:0] ALUResult,
  output ZeroFlag,
  output LessFlag
);

  wire comparator_1_eq, comparator_1_gt, comparator_2_eq, comparator_2_gt, not_1_out, or_2_out, or_3_out,
       RtZero;
  wire [15:0] adder_1_out, and_1_out, bit_extender_1_out, bit_extender_2_out, controlled_buffer_1_out,
       controlled_buffer_2_out, not_2_out, or_1_out, shifter_1_out, shifter_2_out, shifter_3_out,
       shifter_4_out, subtractor_1_out, undriven, undriven_2, xor_1_out;

  assign or_1_out = A | B;  // OR_Gate or_1, 16 bits wide
  assign and_1_out = A & B;  // AND_Gate and_1, 16 bits wide
  assign xor_1_out = A ^ B;  // XOR_Gate xor_1, 16 bits wide
  Adder #(.width(16)) adder_1 (.a(A), .b(B), .out(adder_1_out));  // open: cin, cout
  Subtractor #(.width(16)) subtractor_1 (.a(A), .b(B), .out(subtractor_1_out));  // open: bin, bout
  assign controlled_buffer_1_out = RtZero ? B : 16'bz;  // Controlled_Buffer controlled_buffer_1
  assign controlled_buffer_2_out = not_1_out ? B : 16'bz;  // Controlled_Buffer controlled_buffer_2
  not not_1 (not_1_out, RtZero);
  assign not_2_out = ~and_1_out;  // NOT_Gate not_2, 16 bits wide
  Shifter_part #(.width(16)) shifter_1 (.in(A), .\dist (B[3:0]), .out(shifter_1_out));
  Shifter_part #(.width(16), .shift("lr")) shifter_2 (.in(A), .\dist (B[3:0]), .out(shifter_2_out));
  Shifter_part #(.width(16), .shift("ar")) shifter_3 (.in(A), .\dist (B[3:0]), .out(shifter_3_out));
  Shifter_part #(.width(16), .shift("rr")) shifter_4 (.in(A), .\dist (B[3:0]), .out(shifter_4_out));
  Comparator #(.width(16)) comparator_1 (.a(A), .b(B), .gt(comparator_1_gt), .eq(comparator_1_eq));  // open: lt
  Comparator #(.width(16), .mode("unsigned")) comparator_2 (
    .a(A), .b(B), .gt(comparator_2_gt), .eq(comparator_2_eq));  // open: lt
  or or_2 (or_2_out, comparator_1_gt, comparator_1_eq);
  or or_3 (or_3_out, comparator_2_gt, comparator_2_eq);
  assign bit_extender_1_out = {{15{1'b0}}, or_2_out};  // Bit_Extender bit_extender_1
  assign bit_extender_2_out = {{15{1'b0}}, or_3_out};  // Bit_Extender bit_extender_2
  Multiplexer #(.select(4), .width(16), .enable("false")) multiplexer_1 (
    .in0(or_1_out), .in1(and_1_out), .in2(not_2_out), .in3(xor_1_out), .in4(adder_1_out),
    .in5(subtractor_1_out), .in6(shifter_1_out), .in7(shifter_2_out), .in8(shifter_3_out),
    .in9(shifter_4_out), .in10(bit_extender_1_out), .in11(bit_extender_2_out),
    .in12(controlled_buffer_1_out), .in13(controlled_buffer_2_out), .in14(undriven), .in15(undriven_2),
    .out(ALUResult), .sel(ALUOp));
  Comparator #(.width(16)) comparator_3 (
    .a(subtractor_1_out), .b({16{1'b0}}), .eq(ZeroFlag), .lt(LessFlag));  // open: gt
  or or_4 (RtZero, A[0], A[1], A[2], A[3], A[4], A[5], A[6], A[7], A[8], A[9], A[10], A[11], A[12], A[13], A[14], A[15]);
endmodule

module Shifter (
  input  [15:0] Data,
  input  [3:0] Shift_amount,
  input  [1:0] Shift_Op,
  output [15:0] Data_out
);

  wire [15:0] shifter_1_out, shifter_2_out, shifter_3_out, shifter_4_out;

  Shifter_part #(.width(16)) shifter_1 (.in(Data), .\dist (Shift_amount), .out(shifter_1_out));
  Shifter_part #(.width(16), .shift("lr")) shifter_2 (.in(Data), .\dist (Shift_amount), .out(shifter_2_out));
  Shifter_part #(.width(16), .shift("ar")) shifter_3 (.in(Data), .\dist (Shift_amount), .out(shifter_3_out));
  Shifter_part #(.width(16), .shift("rr")) shifter_4 (.in(Data), .\dist (Shift_amount), .out(shifter_4_out));
  Multiplexer #(.select(2), .width(16), .enable("false")) multiplexer_1 (
    .in0(shifter_1_out), .in1(shifter_2_out), .in2(shifter_3_out), .in3(shifter_4_out), .out(Data_out),
    .sel(Shift_Op));
endmodule

module File_Register (
  input  [2:0] RA,
  input  [2:0] RB,
  input  [2:0] RW,
  input  [15:0] BusW,
  input  RegWrite,
  input  Clock,
  output [15:0] BusA,
  output [15:0] BusB
);

  wire and_1_out, and_2_out, and_3_out, and_4_out, and_5_out, and_6_out, and_7_out, decoder_1_out0,
       decoder_1_out1, decoder_1_out2, decoder_1_out3, decoder_1_out4, decoder_1_out5, decoder_1_out6,
       decoder_1_out7, decoder_2_out0, decoder_2_out1, decoder_2_out2, decoder_2_out3, decoder_2_out4,
       decoder_2_out5, decoder_2_out6, decoder_2_out7, decoder_3_out0, decoder_3_out1, decoder_3_out2,
       decoder_3_out3, decoder_3_out4, decoder_3_out5, decoder_3_out6, decoder_3_out7;
  wire [15:0] R1_q, R2_q, R3_q, R4_q, R5_q, R6_q;

  Decoder #(.select(3), .enable("false")) decoder_1 (
    .out0(decoder_1_out0), .out1(decoder_1_out1), .out2(decoder_1_out2), .out3(decoder_1_out3),
    .out4(decoder_1_out4), .out5(decoder_1_out5), .out6(decoder_1_out6), .out7(decoder_1_out7), .sel(RW));
  Register #(.width(16)) R1 (.D(BusW), .en(and_1_out), .Q(R1_q), .clk(Clock));  // open: clr
  and and_1 (and_1_out, decoder_1_out1, RegWrite);
  Register #(.width(16)) R2 (.D(BusW), .en(and_2_out), .Q(R2_q), .clk(Clock));  // open: clr
  and and_2 (and_2_out, decoder_1_out2, RegWrite);
  Register #(.width(16)) R3 (.D(BusW), .en(and_3_out), .Q(R3_q), .clk(Clock));  // open: clr
  and and_3 (and_3_out, decoder_1_out3, RegWrite);
  Register #(.width(16)) R4 (.D(BusW), .en(and_4_out), .Q(R4_q), .clk(Clock));  // open: clr
  and and_4 (and_4_out, decoder_1_out4, RegWrite);
  Register #(.width(16)) R5 (.D(BusW), .en(and_5_out), .Q(R5_q), .clk(Clock));  // open: clr
  and and_5 (and_5_out, decoder_1_out5, RegWrite);
  Register #(.width(16)) R6 (.D(BusW), .en(and_6_out), .Q(R6_q), .clk(Clock));  // open: clr
  and and_6 (and_6_out, decoder_1_out6, RegWrite);
  Register #(.width(16)) R7 (.D(BusW), .en(and_7_out), .Q(BusA), .clk(Clock));  // open: clr
  and and_7 (and_7_out, decoder_1_out7, RegWrite);
  Decoder #(.select(3), .enable("false")) decoder_2 (
    .out0(decoder_2_out0), .out1(decoder_2_out1), .out2(decoder_2_out2), .out3(decoder_2_out3),
    .out4(decoder_2_out4), .out5(decoder_2_out5), .out6(decoder_2_out6), .out7(decoder_2_out7), .sel(RA));
  assign BusA = decoder_2_out1 ? R1_q : 16'bz;  // Controlled_Buffer controlled_buffer_1
  assign BusA = decoder_2_out2 ? R2_q : 16'bz;  // Controlled_Buffer controlled_buffer_2
  assign BusA = decoder_2_out3 ? R3_q : 16'bz;  // Controlled_Buffer controlled_buffer_3
  assign BusA = decoder_2_out4 ? R4_q : 16'bz;  // Controlled_Buffer controlled_buffer_4
  assign BusA = decoder_2_out5 ? R5_q : 16'bz;  // Controlled_Buffer controlled_buffer_5
  assign BusA = decoder_2_out6 ? R6_q : 16'bz;  // Controlled_Buffer controlled_buffer_6
  assign BusA = decoder_2_out7 ? BusA : 16'bz;  // Controlled_Buffer controlled_buffer_7
  assign BusA = decoder_2_out0 ? {16{1'b0}} : 16'bz;  // Controlled_Buffer controlled_buffer_8
  Decoder #(.select(3), .enable("false")) decoder_3 (
    .out0(decoder_3_out0), .out1(decoder_3_out1), .out2(decoder_3_out2), .out3(decoder_3_out3),
    .out4(decoder_3_out4), .out5(decoder_3_out5), .out6(decoder_3_out6), .out7(decoder_3_out7), .sel(RB));
  assign BusB = decoder_3_out0 ? {16{1'b0}} : 16'bz;  // Controlled_Buffer controlled_buffer_9
  assign BusB = decoder_3_out1 ? R1_q : 16'bz;  // Controlled_Buffer controlled_buffer_10
  assign BusB = decoder_3_out2 ? R2_q : 16'bz;  // Controlled_Buffer controlled_buffer_11
  assign BusB = decoder_3_out3 ? R3_q : 16'bz;  // Controlled_Buffer controlled_buffer_12
  assign BusB = decoder_3_out4 ? R4_q : 16'bz;  // Controlled_Buffer controlled_buffer_13
  assign BusB = decoder_3_out5 ? R5_q : 16'bz;  // Controlled_Buffer controlled_buffer_14
  assign BusB = decoder_3_out6 ? R6_q : 16'bz;  // Controlled_Buffer controlled_buffer_15
  assign BusB = decoder_3_out7 ? BusA : 16'bz;  // Controlled_Buffer controlled_buffer_16
endmodule

module PC_Control (
  input  [3:0] Opcode,
  input  ZeroFlag,
  input  LessFlag,
  output [1:0] PCSrc
);

  wire and_1_out, and_2_out, and_3_out, and_4_out, and_5_out, and_6_out, and_7_out, Branch, decoder_1_out7,
       decoder_1_out8, decoder_1_out9, decoder_1_out10, decoder_1_out11, decoder_1_out12, JR_JALR, Jump,
       Jump1, not_1_out, not_2_out, or_3_out;
  wire [1:0] or_4_out;

  Decoder #(.select(4), .enable("false")) decoder_1 (
    .out1(JR_JALR), .out7(decoder_1_out7), .out8(decoder_1_out8), .out9(decoder_1_out9),
    .out10(decoder_1_out10), .out11(decoder_1_out11), .out12(decoder_1_out12), .out14(Jump), .out15(Jump1),
    .sel(Opcode));  // open: out0, out2, out3, out4, out5, out6, out13
  not not_1 (not_1_out, ZeroFlag);
  not not_2 (not_2_out, LessFlag);
  and and_1 (and_1_out, ZeroFlag, decoder_1_out12);
  and and_2 (and_2_out, LessFlag, decoder_1_out12);
  and and_3 (and_3_out, LessFlag, decoder_1_out11);
  and and_4 (and_4_out, not_2_out, decoder_1_out10);
  and and_5 (and_5_out, not_2_out, not_1_out, decoder_1_out9);
  and and_6 (and_6_out, decoder_1_out8, ZeroFlag);
  and and_7 (and_7_out, not_1_out, decoder_1_out7);
  or or_1 (Branch, and_1_out, and_2_out, and_3_out, and_4_out, and_5_out, and_6_out, and_7_out);
  or or_2 (or_4_out[1], Branch, JR_JALR);
  or or_3 (or_3_out, Jump1, Jump);
  or or_4 (or_4_out[0], or_3_out, JR_JALR);
  Multiplexer #(.select(2), .width(2), .enable("false")) multiplexer_1 (
    .in0(2'b00), .in1(2'b01), .in2(2'b10), .in3(2'b11), .out(PCSrc), .sel(or_4_out));

  // Notes on the sheet:
  //   01
  //   10
  //   11
  //   00
endmodule

module Main_Control (
  input  [3:0] Opcode,
  input  [2:0] Funct,
  output RegDst,
  output MemWr,
  output MemRd,
  output [1:0] WBdata,
  output ExtOp,
  output ALUSrc,
  output RegWr
);

  wire _0, _1, _2, _3, _4, _13, _15, and_1_out, and_2_out, and_3_out, and_4_out, and_5_out, not_1_out,
       or_3_out;

  or or_1 (RegDst, _0, _13, _1);
  or or_2 (RegWr, _0, _1, _2, _3, _4, MemRd, _13, _15);
  and and_1 (and_1_out, Funct[0], Funct[1], Funct[2]);
  not not_1 (not_1_out, Opcode[1]);
  Decoder #(.select(4), .enable("false")) decoder_1 (
    .out0(_0), .out1(_1), .out2(_2), .out3(_3), .out4(_4), .out5(MemWr), .out6(MemRd), .out13(_13),
    .out15(_15), .sel(Opcode));  // open: out7, out8, out9, out10, out11, out12, out14
  and and_2 (and_2_out, Opcode[0], Opcode[1], Opcode[2], Opcode[3]);
  and and_3 (and_3_out, Opcode[0], ~Opcode[1], ~Opcode[2], ~Opcode[3]);  // AND_Gate
  and and_4 (and_4_out, and_3_out, and_1_out);
  and and_5 (and_5_out, Opcode[0], not_1_out, Opcode[2], Opcode[3]);
  or or_3 (or_3_out, and_2_out, and_4_out);
  Priority_Encoder #(.select(2), .disabled(0)) priority_encoder_1 (
    .in0(1'b1), .in1(or_3_out), .in2(and_5_out), .in3(MemRd), .out(WBdata));  // open: gs, en_out, en_in
  nor nor_1 (ExtOp, _2, _3, _13);
  or or_4 (ALUSrc, _2, _3, _4, MemWr, MemRd, _13);

  // Other names for the same wires on the sheet: _5 = MemWr; _6 = MemRd
endmodule

module ALU_Control (
  input  [3:0] Opcode,
  input  [2:0] Funct,
  output [3:0] ALUOp
);

  wire and_1_out, and_2_out, and_3_out, and_4_out, and_5_out, and_6_out, and_7_out, and_8_out, and_9_out,
       and_10_out, and_11_out, not_1_out, not_2_out, not_3_out, not_4_out, not_5_out, not_6_out, not_7_out,
       not_8_out, not_9_out, not_10_out, not_11_out, not_12_out, not_13_out, not_14_out, not_15_out,
       not_16_out, not_17_out, not_18_out, not_19_out, not_20_out, not_21_out, not_22_out, not_23_out;

  not not_1 (not_1_out, Opcode[3]);
  not not_2 (not_2_out, Opcode[2]);
  not not_3 (not_3_out, Opcode[1]);
  not not_4 (not_4_out, Opcode[3]);
  not not_5 (not_5_out, Opcode[1]);
  not not_6 (not_6_out, Opcode[3]);
  not not_7 (not_7_out, Opcode[1]);
  not not_8 (not_8_out, Opcode[1]);
  not not_9 (not_9_out, Opcode[1]);
  not not_10 (not_10_out, Funct[1]);
  not not_11 (not_11_out, Opcode[1]);
  not not_12 (not_12_out, Funct[1]);
  not not_13 (not_13_out, Opcode[3]);
  not not_14 (not_14_out, Opcode[2]);
  not not_15 (not_15_out, Opcode[1]);
  not not_16 (not_16_out, Opcode[0]);
  not not_17 (not_17_out, Opcode[3]);
  not not_18 (not_18_out, Opcode[1]);
  not not_19 (not_19_out, Funct[2]);
  not not_20 (not_20_out, Funct[1]);
  not not_21 (not_21_out, Opcode[2]);
  not not_22 (not_22_out, Opcode[1]);
  not not_23 (not_23_out, Opcode[0]);
  and and_1 (and_1_out, not_1_out, not_2_out, not_3_out, Funct[2], Funct[1]);
  and and_2 (and_2_out, not_4_out, not_5_out, Opcode[0], Funct[1]);
  and and_3 (and_3_out, not_6_out, not_7_out, Opcode[0], Funct[2]);
  and and_4 (and_4_out, Opcode[2], not_8_out, Opcode[0]);
  and and_5 (and_5_out, not_9_out, Funct[2], not_10_out);
  and and_6 (and_6_out, not_11_out, Opcode[0], not_12_out);
  and and_7 (and_7_out, not_13_out, not_14_out, not_15_out, not_16_out, Funct[1]);
  and and_8 (and_8_out, not_17_out, not_18_out, Opcode[0], not_19_out, not_20_out);
  and and_9 (and_9_out, not_21_out, not_22_out, Funct[0]);
  and and_10 (and_10_out, Opcode[1], not_23_out);
  and and_11 (and_11_out, Opcode[2], Opcode[1]);
  or or_1 (ALUOp[3], and_1_out, and_2_out, and_3_out, and_4_out);
  or or_2 (ALUOp[1], and_5_out, and_6_out, Opcode[2], Opcode[3]);
  or or_3 (ALUOp[2], and_7_out, and_8_out);
  or or_4 (ALUOp[0], and_9_out, and_10_out, and_11_out, Opcode[3]);
endmodule
